# Fritzing sketch VSR_Hands (saved by Fritzing 0.9.3b)

parts:
  Part1 = SRF05 Ultrasonic Rangefinder
  J1 = Basic Servo
  J2 = Basic Servo
  Part2 = Arduino Nano (Rev3.0)
  VCC1 = Battery

nets:
  VCC: Part1.VCC, Part2.5V
  N1: Part1.Trig, Part2.D7
  N2: Part1.Echo, Part2.D6
  GND: Part1.GND, Part2.GND
  GND_2: J1.gnd, J2.gnd, Part2.D0/RX, VCC1.-
  N3: J1.pulse, Part2.D9
  N4: J2.pulse, Part2.D10
