# Fritzing sketch VSR_Navigation_1 (saved by Fritzing 0.9.3b)

parts:
  Part1 = SRF05 Ultrasonic Rangefinder
  Part3 = SRF05 Ultrasonic Rangefinder
  Part5 = SRF05 Ultrasonic Rangefinder
  U2 = Module 4 Relais 5V [package="Module 4 Relais 5V"]
  Part6 = Arduino Nano (Rev3.0)
  M1 = DC Motor
  M2 = DC Motor
  VCC1 = Battery

nets:
  VCC: Part1.VCC, Part6.5V
  N1: Part1.Trig, Part6.D6
  N2: Part1.Echo, Part6.D7
  GND: Part1.GND, Part6.GND
  N3: Part3.Trig, Part6.D4
  N4: Part3.Echo, Part6.D5
  N5: Part5.Trig, Part6.D2
  N6: Part5.Echo, Part6.D3
  N7: U2.IN1, Part6.D8
  N8: U2.IN2, Part6.D9
  N9: U2.IN3, Part6.D10
  N10: U2.IN4, Part6.D11/MOSI
  N11: U2.K2-NF, M1.pin_1
  N12: U2.K3-NF, M2.pin_1
  N13: U2.K4-NF, U2.K2-NO, VCC1.+

custom parts:
  Module 4 Relais 5V: Module 4 Relais 5V 4x SPD-06VDC-SD-C
