# Fritzing sketch VSR_Sanitizer (saved by Fritzing 0.9.3b)

parts:
  U2 = Module 4 Relais 5V [package="Module 4 Relais 5V"]
  BAT1 = 18650 battery holder [package=battery-18650-kit]
  WATER_PUMP1 = water pump/motor  # not connected
  hc-sr1 = hc-sr04
  Part1 = Arduino Nano (Rev3.0)

nets:
  VCC: U2.VCC, Part1.5V
  GND: U2.GND, hc-sr1.GND, Part1.GND
  N1: U2.IN1, Part1.D8
  N2: U2.K1-NO, BAT1.+
  VCC_2: hc-sr1.VCC, Part1.3V3
  N3: hc-sr1.Trig, Part1.D5
  N4: hc-sr1.Echo, Part1.D4

custom parts:
  Module 4 Relais 5V: Module 4 Relais 5V 4x SPD-06VDC-SD-C
  18650 battery holder: 18650 Battery Holder
  water pump/motor: WATER PUMP BY ARDUBLOCKTR

// code stored in the sketch: blink_LED.ino
void setup() {
  // initialize digital pin LED_BUILTIN as an output.
  pinMode(LED_BUILTIN, OUTPUT);
}

// the loop function runs over and over again forever
void loop() {
  digitalWrite(LED_BUILTIN, HIGH);   // turn the LED on (HIGH is the voltage level)
  delay(1000);                       // wait for a second
  digitalWrite(LED_BUILTIN, LOW);    // turn the LED off by making the voltage LOW
  delay(1000);                       // wait for a second
}
