# Fritzing sketch VSR_Solar_Pannel (saved by Fritzing 0.9.3b)

parts:
  Part1 = Arduino Nano (Rev3.0)
  DHT1 = Humidity and Temperature Sensor DHT11
  U1 = Module 4 Relais 5V [package="Module 4 Relais 5V"]
  BAT1 = 18650 battery holder [package=battery-18650-kit]
  M1 = Stepper Motor - Bipolar

nets:
  GND: Part1.GND, DHT1.GND_1, U1.GND
  N1: Part1.D2, DHT1.Data-signal
  N2: Part1.D9, U1.IN4
  N3: Part1.D10, U1.IN1
  N4: Part1.D11/MOSI, U1.IN2
  N5: Part1.D12/MISO, U1.IN3
  5V: Part1.5V, U1.VCC
  3V3: Part1.3V3, DHT1.Vcc
  N6: U1.K1-NO, BAT1.+
  N7: U1.K2-NO, BAT1.-
  N8: M1.A, M1.B
  N9: M1.C, M1.D

custom parts:
  Humidity and Temperature Sensor DHT11: Digital relative humidity & temperature sensor DHT11
  Module 4 Relais 5V: Module 4 Relais 5V 4x SPD-06VDC-SD-C
  18650 battery holder: 18650 Battery Holder
