# Fritzing sketch VSRSwitching_Portal (saved by Fritzing 0.9.3b)

parts:
  U1 = Module 4 Relais 5V [package="Module 4 Relais 5V"]
  U2 = ESP8266 NodeMCU LoLin module
  U3 = Module 4 Relais 5V [package="Module 4 Relais 5V"]
  BAT1 = 18650 battery holder [package=battery-18650-kit]
  M1 = DC Motor
  M2 = DC Motor
  ANT1 = Antenna
  ANT2 = Antenna
  VCC1 = Battery

nets:
  VCC: U1.VCC, U2.Vin
  GND: U1.GND, U2.GND
  N1: U1.IN1, U2.D1
  N2: U1.IN2, U2.D2
  N3: U1.IN3, U2.D3
  N4: U1.IN4, U2.D4
  N5: U1.K1-NF, M2.pin_1
  N6: U1.K2-NF, M1.pin_1
  N7: U1.K3-NF, M2.pin_2
  N8: U1.K4-NF, M1.pin_2
  N9: U1.K4-Com, BAT1.-
  N10: U1.K3-NO, BAT1.+
  N11: U2.D5, U3.IN1
  N12: U2.D7, U3.IN2
  N13: U3.K3-NF, ANT2.antenna_lead
  N14: U3.K4-NF, ANT1.antenna_lead
  N15: U3.K3-NO, VCC1.-
  N16: U3.K4-NO, VCC1.+

custom parts:
  Module 4 Relais 5V: Module 4 Relais 5V 4x SPD-06VDC-SD-C
  ESP8266 NodeMCU LoLin module: ESP8266 based NodeMCU
  18650 battery holder: 18650 Battery Holder

// code stored in the sketch: blink_LED.ino
void setup() {
  // initialize digital pin LED_BUILTIN as an output.
  pinMode(LED_BUILTIN, OUTPUT);
}

// the loop function runs over and over again forever
void loop() {
  digitalWrite(LED_BUILTIN, HIGH);   // turn the LED on (HIGH is the voltage level)
  delay(1000);                       // wait for a second
  digitalWrite(LED_BUILTIN, LOW);    // turn the LED off by making the voltage LOW
  delay(1000);                       // wait for a second
}
