# Fritzing sketch VSR_akabati (saved by Fritzing 0.9.3b)

parts:
  U2 = Module 4 Relais 5V [package="Module 4 Relais 5V"]
  BAT1 = 18650 battery holder [package=battery-18650-kit]
  M1 = DC Motor
  M2 = DC Motor
  Part1 = Arduino Nano (Rev3.0)
  hc-sr1 = hc-sr04

nets:
  VCC: U2.VCC, Part1.5V
  GND: U2.GND, Part1.GND, hc-sr1.GND
  N1: U2.IN1, Part1.D8
  N2: U2.IN2, Part1.D9
  N3: U2.K1-NO, BAT1.-
  N4: U2.K2-NO, BAT1.+
  N5: M1.pin_1, M2.pin_1
  N6: M1.pin_2, M2.pin_2
  N7: Part1.D4, hc-sr1.Echo
  N8: Part1.D5, hc-sr1.Trig
  3V3: Part1.3V3, hc-sr1.VCC

custom parts:
  Module 4 Relais 5V: Module 4 Relais 5V 4x SPD-06VDC-SD-C
  18650 battery holder: 18650 Battery Holder

// code stored in the sketch: blink_LED.ino
void setup() {
  // initialize digital pin LED_BUILTIN as an output.
  pinMode(LED_BUILTIN, OUTPUT);
}

// the loop function runs over and over again forever
void loop() {
  digitalWrite(LED_BUILTIN, HIGH);   // turn the LED on (HIGH is the voltage level)
  delay(1000);                       // wait for a second
  digitalWrite(LED_BUILTIN, LOW);    // turn the LED off by making the voltage LOW
  delay(1000);                       // wait for a second
}
